# Fritzing sketch blind_spot (saved by Fritzing 0.7.0b)
breadboards: 1

parts:
  Master = Arduino
  Slave = Arduino
  R1 = Resistor [tolerance=±5% resistance=1k package="0603 [SMD]"]
  R3 = Resistor [tolerance=±5% resistance=1k package="0603 [SMD]"]
  R4 = Resistor [tolerance=±5% resistance=1k package="0603 [SMD]"]
  R5 = Resistor [tolerance=±5% resistance=1k package="0603 [SMD]"]
  LCD = LCD screen
  R6 = Resistor [tolerance=±5% resistance=1k package="0603 [SMD]"]
  R7 = Resistor [tolerance=±5% resistance=1k package="0603 [SMD]"]
  Primary_Sensor = SRF05 Ultrasonic Rangefinder
  Motor_Driver = H-Bridge [package=THT]
  Power_Supply_for_Motors = Battery block 9V
  Power_Supply_for_Arduino = Battery block 9V
  Front/Back = DC Motor
  Left/Right = DC Motor
  LED1 = LED - 5mm [color="Red (633nm)" package="5 mm [THT]"]
  R8 = Resistor [tolerance=±5% resistance=220 package="0805 [SMD]"]
  Xbee_Adapter = DIP - 4 pins [package="DIP (Dual Inline) [THT]"]
  Secondary_Sensor = DIP - 4 pins [package="DIP (Dual Inline) [THT]"]

nets:
  GND: Master.GND, Slave.GND, LCD.VSS, LCD.R/W, Primary_Sensor.Ground, Motor_Driver.GND1, Motor_Driver.GND2, Motor_Driver.GND3, Motor_Driver.GND4, Power_Supply_for_Motors.-, LED1.cathode, Xbee_Adapter.GND, Secondary_Sensor.GND
  N1: Master.D13, Primary_Sensor.Trigger_Input
  N2: Master.D12, Primary_Sensor.Echo_Output
  N3: Master.D11, R8.Pin_0
  N4: Master.D9, LCD.RS
  N5: Master.D8, LCD.E
  N6: Master.D7, LCD.DB4
  N7: Master.D4, LCD.DB5
  N8: Master.D3, LCD.DB6
  N9: Master.D2, LCD.DB7
  N10: Master.D1TX, Xbee_Adapter.RX
  N11: Master.D0RX, Xbee_Adapter.TX
  +5V: Master.+5V, Slave.+5V, R3.Pin_0, R5.Pin_0, Motor_Driver.VCC1, Power_Supply_for_Arduino.+, Xbee_Adapter.5V, Secondary_Sensor.VCC
  N12: Master.A0, Secondary_Sensor.V0
  N13: Master.A4, Slave.A4, R4.Pin_1
  N14: Master.A5, Slave.A5, R1.Pin_1, Power_Supply_for_Arduino.-
  N15: Slave.D12, Motor_Driver.1A
  N16: Slave.D11, Motor_Driver.1_2EN
  N17: Slave.D10, Motor_Driver.2A
  N18: Slave.D4, Motor_Driver.4A
  N19: Slave.D3, Motor_Driver.3_4EN
  N20: Slave.D2, Motor_Driver.3A
  N21: R1.Pin_0, R3.Pin_1
  N22: R4.Pin_0, R5.Pin_1
  N23: LCD.V0, R6.Pin_0, R7.Pin_0
  N24: R6.Pin_1, R7.Pin_1
  N25: Motor_Driver.1Y, Front/Back.pin_1
  N26: Motor_Driver.2Y, Front/Back.pin_2
  N27: Motor_Driver.VCC2, Power_Supply_for_Motors.+
  N28: Motor_Driver.3Y, Left/Right.pin_2
  N29: Motor_Driver.4Y, Left/Right.pin_1
  N30: LED1.anode, R8.Pin_1

custom parts:
  DIP - 4 pins: A DIP stand-in part for whatever IC you want. With 4 pins on a 300 mil dual inline package (DIP) footprint.
  DIP - 4 pins: A DIP stand-in part for whatever IC you want. With 4 pins on a 300 mil dual inline package (DIP) footprint.
